# Fritzing sketch Communicate-with-NodeMCU-via-ArduinoUnoR3 (saved by Fritzing 0.9.3b)
breadboards: 1

parts:
  Part1 = Arduino Uno (Rev3)
  U1 = NodeMCU V1.0  # not connected
  Part2 = Logic Level Converter

nets:
  N1: Part1.5V, Part2.HV
  GND: Part1.GND, Part2.GND

custom parts:
  NodeMCU V1.0: ESP8266 based NodeMCU
